# Fritzing sketch WALL-E DIAGRAM (saved by Fritzing 0.9.3b)
breadboards: 2

parts:
  Raspberry_Pi_1 = Raspberry Pi 3 [part_number=RPI-3-V1.2]
  HC-05_bluetooth = Bluetooth HC-05 Macho
  R1 = Resistor [tolerance=±5% resistance=2.2k package="0603 [SMD]"]
  R2 = Resistor [tolerance=±5% resistance=4.7k package="0603 [SMD]"]
  SM1 = 28BYJ-48 Stepper Motor [part_number=28BYJ-48]
  Driver1 = 28BYJ-48 Driver Module [part_number=ULN2003 package=THT]
  Driver2 = 28BYJ-48 Driver Module [part_number=ULN2003 package=THT]
  SM2 = 28BYJ-48 Stepper Motor [part_number=28BYJ-48]
  SERVO_MOTOR = Basic Servo  # not connected
  Driver3 = 28BYJ-48 Driver Module [part_number=ULN2003 package=THT]
  SM3 = 28BYJ-48 Stepper Motor [part_number=28BYJ-48]
  Driver4 = 28BYJ-48 Driver Module [part_number=ULN2003 package=THT]
  SM4 = 28BYJ-48 Stepper Motor [part_number=28BYJ-48]
  Driver5 = 28BYJ-48 Driver Module [part_number=ULN2003 package=THT]
  SM5 = 28BYJ-48 Stepper Motor [part_number=28BYJ-48]
  M1 = fc-51 [package=THT]  # not connected
  IR_SENSOR = fc-51 [package=THT]  # not connected
  M3 = fc-51 [package=THT]  # not connected
  Part1 = Arduino Mega ADK (Rev3)
  RGB_LED_MODULE = KY-016 RGB Full Color LED Module [package="Breakout board"]  # not connected
  SERVO_MOTOR_2 = Basic Servo  # not connected
  RGB_LED_MODULE_2 = KY-016 RGB Full Color LED Module [package="Breakout board"]  # not connected
  Mod3 = KY-016 RGB Full Color LED Module [package="Breakout board"]  # not connected
  YwRobot_Power_Supply1 = YwRobot Breadboard Power Supply [part_number=545043]  # not connected
  OLED_I2C1 = OLED 128x64 I2C Monochrome Display  # not connected
  Q1 = TRANSISTOR_NPN [package=to-92-ammo]  # not connected
  M4 = Max30205 body temp sensor [package=THT]  # not connected

nets:
  N1: Raspberry_Pi_1.GND, Raspberry_Pi_1.GIPO18
  N2: HC-05_bluetooth.TXD, Part1.D9_PWM
  N3: HC-05_bluetooth.RXD, R1.Pin_1, R2.Pin_0
  VCC: HC-05_bluetooth.VCC, Part1.5V
  GND: HC-05_bluetooth.GND, R2.Pin_1, Part1.GND
  N4: R1.Pin_0, Part1.D8_PWM
  N5: SM1.blue-pin, Driver1.blue-pin
  N6: SM1.pink-pin, Driver1.pink-pin
  N7: SM1.yellow-pin, Driver1.yellow-pin
  N8: SM1.orange-pin, Driver1.orange-pin
  N9: SM1.red-pin, Driver1.red-pin
  N10: Driver2.blue-pin, SM2.blue-pin
  N11: Driver2.pink-pin, SM2.pink-pin
  N12: Driver2.yellow-pin, SM2.yellow-pin
  N13: Driver2.orange-pin, SM2.orange-pin
  N14: Driver2.red-pin, SM2.red-pin
  N15: Driver3.blue-pin, SM3.blue-pin
  N16: Driver3.pink-pin, SM3.pink-pin
  N17: Driver3.yellow-pin, SM3.yellow-pin
  N18: Driver3.orange-pin, SM3.orange-pin
  N19: Driver3.red-pin, SM3.red-pin
  N20: Driver4.blue-pin, SM4.blue-pin
  N21: Driver4.pink-pin, SM4.pink-pin
  N22: Driver4.yellow-pin, SM4.yellow-pin
  N23: Driver4.orange-pin, SM4.orange-pin
  N24: Driver4.red-pin, SM4.red-pin
  N25: Driver5.blue-pin, SM5.blue-pin
  N26: Driver5.pink-pin, SM5.pink-pin
  N27: Driver5.yellow-pin, SM5.yellow-pin
  N28: Driver5.orange-pin, SM5.orange-pin
  N29: Driver5.red-pin, SM5.red-pin

notes:
  Resistor 1 : 2.2k
  Resistor 2 : 5.7k
  Audio Jack : For Speaker
  USB 2x : For microphone
  Ethernet : For Internet Connection
  Camera : For Recording Face
  Used for left wheel
  Used for right wheel
  Used for change direction
  Used for pill dispenser
  Used for pill dispenser fall detection
  MAX30205 or Transistor used for temperature identification
  LINK :
  - Arduino Based Digital Thermometer using MAX30205 Human Body Temperature Sensor
  - Arduino Temperature Sensor Using LM35 : 3 Steps - Instructables
  Used for connection to raspberry pi
  Used for med schedule sa led or light indicator in ubos na med or wala pwedeng yung sa sceen ai na rin
  Used for locking system
  LINK :
  - Simple Door Lock Diy
  Used for eyes, just emit light for emotions
  Used for extra power supply to any components
  Used for mini display

custom parts:
  28BYJ-48 Stepper Motor: Unipolar Stepper Motor 28BYJ-48 Top coil - pink & orange Bottom coil - blue & yellow Common rail - red Connector pins: blue - pink - yellow - orange - red
  28BYJ-48 Driver Module: ULN2003 Driver Module for the 28BYJ-48 Unipolar Stepper Motor LED A - Blue wire - Bottom coil left LED B - Pink wire - Top coil left LED C - Yellow wire - Bottom coil right LED D - Orange wire - Top coil right Common rail - red Connector pins: blue - pink - yellow - orange - red Control pins - IN1 to IN4 Power pins - GND & Vmotor (5-12V) On/Off jumper (if removed, power to motor is cut).
  KY-016 RGB Full Color LED Module: KY-016 Arduino full color 5mm RGB LED, different colors can be obtained by mixing the three primary colors.
  YwRobot Breadboard Power Supply: The YwRobot Breadboard Power Supply (MB-V2) has two power rails; they can be 5V or 3V3. Power to the module can be provided through the female USB socket or through the A10 (female) 2.1mm power jack.
  Max30205 body temp sensor: This module is based on MAX30205 which is a temperature sensor that accurately measures temperature and provides an over-temperature alarm/interrupt/shutdown output.
